// Logisim project Offline 1.circ as structural Verilog: 1 circuit, main circuit Organized
module Organized (
  input  CS2,
  input  CS1,
  input  CS0,
  input  A3,
  input  A2,
  input  A1,
  input  A0,
  input  B3,
  input  B2,
  input  B1,
  input  B0,
  output S3,
  output S2,
  output S1,
  output S0,
  output S,
  output V,
  output C,
  output Z
);

  wire Ad0__6__s2, Ad1__6__s2, Ad2__6__s2, Ad3__6__s2, AND1__3__1y, AND1__6__2y, AND1__8__3y, AND1__11__4y,
       AND2__3__1y, AND2__6__2y, AND2__8__3y, AND2__11__4y, B_prime_F2__3__1y, B_prime_F2__6__2y,
       B_prime_F2__8__3y, B_prime_F2__11__4y, B_prime_S1S0_prime__3__1y, B_prime_S1S0_prime__6__2y,
       B_prime_S1S0_prime__8__3y, B_prime_S1S0_prime__11__4y, BF1__3__1y, BF1__6__2y, BF1__8__3y,
       BF1__11__4y, n7408_1__3__1y, n7408_1__6__2y, n7408_1__11__4y, NOT1__2__1y, NOT1__4__2y, NOT1__6__3y,
       NOT1__8__4y, NOT1__10__5y, NOT1__12__6y, OR1__3__1y, OR1__6__2y, SOR__3__1y, SOR__6__2y, SOR__11__4y,
       SRNOT__2__1y, SRNOT__4__2y, X__3__1y, X__6__2y, X__8__3y, X__11__4y, Y__3__1y, Y__6__2y, Y__8__3y,
       Y__11__4y;

  _7404 NOT1 (
    ._1__1A(CS1), ._2__1Y(NOT1__2__1y), ._3__2A(CS0), ._4__2Y(NOT1__4__2y), ._5__3A(B0),
    ._6__3Y(NOT1__6__3y), ._13__6A(B3), ._12__6Y(NOT1__12__6y), ._11__5A(B2), ._10__5Y(NOT1__10__5y),
    ._9__4A(B1), ._8__4Y(NOT1__8__4y));  // open: _7__GND, _14__Vcc
  _7408 AND1 (
    ._1__1A(CS1), ._2__1B(CS0), ._3__1Y(AND1__3__1y), ._4__2A(NOT1__2__1y), ._5__2B(NOT1__4__2y),
    ._6__2Y(AND1__6__2y), ._13__4B(CS0), ._12__4A(CS2), ._11__4Y(AND1__11__4y), ._10__3B(CS1),
    ._9__3A(NOT1__4__2y), ._8__3Y(AND1__8__3y));  // open: _7__GND, _14__Vcc
  _7432 OR1 (
    ._1__1A(AND1__6__2y), ._2__1B(AND1__3__1y), ._3__1Y(OR1__3__1y), ._4__2A(AND1__8__3y),
    ._5__2B(AND2__3__1y), ._6__2Y(OR1__6__2y), ._13__4B(AND2__6__2y), ._12__4A(AND2__8__3y), ._11__4Y(V));  // open: _7__GND, _14__Vcc, _10__3B, _9__3A, _8__3Y
  _7408 AND2 (
    ._1__1A(AND1__11__4y), ._2__1B(NOT1__2__1y), ._3__1Y(AND2__3__1y), ._4__2A(n7408_1__11__4y),
    ._5__2B(SRNOT__2__1y), ._6__2Y(AND2__6__2y), ._13__4B(CS1), ._12__4A(AND1__11__4y),
    ._11__4Y(AND2__11__4y), ._10__3B(C), ._9__3A(SRNOT__4__2y), ._8__3Y(AND2__8__3y));  // open: _7__GND, _14__Vcc
  _7408 B_prime_F2 (
    ._1__1A(OR1__6__2y), ._2__1B(NOT1__6__3y), ._3__1Y(B_prime_F2__3__1y), ._4__2A(OR1__6__2y),
    ._5__2B(NOT1__8__4y), ._6__2Y(B_prime_F2__6__2y), ._13__4B(OR1__6__2y), ._12__4A(NOT1__12__6y),
    ._11__4Y(B_prime_F2__11__4y), ._10__3B(OR1__6__2y), ._9__3A(NOT1__10__5y), ._8__3Y(B_prime_F2__8__3y));  // open: _7__GND, _14__Vcc
  _7408 BF1 (
    ._1__1A(B0), ._2__1B(OR1__3__1y), ._3__1Y(BF1__3__1y), ._4__2A(B1), ._5__2B(OR1__3__1y),
    ._6__2Y(BF1__6__2y), ._13__4B(B3), ._12__4A(OR1__3__1y), ._11__4Y(BF1__11__4y), ._10__3B(B2),
    ._9__3A(OR1__3__1y), ._8__3Y(BF1__8__3y));  // open: _7__GND, _14__Vcc
  _7432 Y (
    ._1__1A(BF1__3__1y), ._2__1B(B_prime_F2__3__1y), ._3__1Y(Y__3__1y), ._4__2A(BF1__6__2y),
    ._5__2B(B_prime_F2__6__2y), ._6__2Y(Y__6__2y), ._13__4B(BF1__11__4y), ._12__4A(B_prime_F2__11__4y),
    ._11__4Y(Y__11__4y), ._10__3B(BF1__8__3y), ._9__3A(B_prime_F2__8__3y), ._8__3Y(Y__8__3y));  // open: _7__GND, _14__Vcc
  _7408 B_prime_S1S0_prime (
    ._1__1A(NOT1__6__3y), ._2__1B(AND1__8__3y), ._3__1Y(B_prime_S1S0_prime__3__1y), ._4__2A(NOT1__8__4y),
    ._5__2B(AND1__8__3y), ._6__2Y(B_prime_S1S0_prime__6__2y), ._13__4B(NOT1__12__6y), ._12__4A(AND1__8__3y),
    ._11__4Y(B_prime_S1S0_prime__11__4y), ._10__3B(NOT1__10__5y), ._9__3A(AND1__8__3y),
    ._8__3Y(B_prime_S1S0_prime__8__3y));  // open: _7__GND, _14__Vcc
  _7432 X (
    ._1__1A(A0), ._2__1B(B_prime_S1S0_prime__3__1y), ._3__1Y(X__3__1y), ._4__2A(A1),
    ._5__2B(B_prime_S1S0_prime__6__2y), ._6__2Y(X__6__2y), ._13__4B(A3),
    ._12__4A(B_prime_S1S0_prime__11__4y), ._11__4Y(X__11__4y), ._10__3B(A2),
    ._9__3A(B_prime_S1S0_prime__8__3y), ._8__3Y(X__8__3y));  // open: _7__GND, _14__Vcc
  _7483 Ad0 (
    ._1__A4(1'b0), ._3__A3(1'b0), ._4__B3(1'b0), ._6__S2(Ad0__6__s2), ._7__B2(1'b0), ._8__A2(1'b0),
    ._16__B4(1'b0), ._13__Cin(AND2__11__4y), ._11__B1(X__3__1y), ._10__A1(Y__3__1y), ._9__S1(S0));  // open: _2__S3, _5__Vcc, _15__S4, _14__Cout, _12__GND
  _7483 Ad1 (
    ._1__A4(1'b0), ._3__A3(1'b0), ._4__B3(1'b0), ._6__S2(Ad1__6__s2), ._7__B2(1'b0), ._8__A2(1'b0),
    ._16__B4(1'b0), ._13__Cin(n7408_1__3__1y), ._11__B1(X__6__2y), ._10__A1(Y__6__2y), ._9__S1(S1));  // open: _2__S3, _5__Vcc, _15__S4, _14__Cout, _12__GND
  _7483 Ad2 (
    ._1__A4(1'b0), ._3__A3(1'b0), ._4__B3(1'b0), ._6__S2(Ad2__6__s2), ._7__B2(1'b0), ._8__A2(1'b0),
    ._16__B4(1'b0), ._13__Cin(n7408_1__6__2y), ._11__B1(X__8__3y), ._10__A1(Y__8__3y), ._9__S1(S2));  // open: _2__S3, _5__Vcc, _15__S4, _14__Cout, _12__GND
  _7483 Ad3 (
    ._1__A4(1'b0), ._3__A3(1'b0), ._4__B3(1'b0), ._6__S2(Ad3__6__s2), ._7__B2(1'b0), ._8__A2(1'b0),
    ._16__B4(1'b0), ._13__Cin(n7408_1__11__4y), ._11__B1(X__11__4y), ._10__A1(Y__11__4y), ._9__S1(S));  // open: _2__S3, _5__Vcc, _15__S4, _14__Cout, _12__GND
  _7408 u_7408_1 (
    ._1__1A(CS0), ._2__1B(Ad0__6__s2), ._3__1Y(n7408_1__3__1y), ._4__2A(CS0), ._5__2B(Ad1__6__s2),
    ._6__2Y(n7408_1__6__2y), ._13__4B(CS0), ._12__4A(Ad2__6__s2), ._11__4Y(n7408_1__11__4y), ._10__3B(CS0),
    ._9__3A(Ad3__6__s2), ._8__3Y(C));  // open: _7__GND, _14__Vcc
  _7404 SRNOT (
    ._1__1A(C), ._2__1Y(SRNOT__2__1y), ._3__2A(n7408_1__11__4y), ._4__2Y(SRNOT__4__2y), ._9__4A(SOR__11__4y),
    ._8__4Y(Z));  // open: _5__3A, _6__3Y, _7__GND, _14__Vcc, _13__6A, _12__6Y, _11__5A, _10__5Y
  _7432 SOR (
    ._1__1A(S), ._2__1B(S2), ._3__1Y(SOR__3__1y), ._4__2A(S1), ._5__2B(S0), ._6__2Y(SOR__6__2y),
    ._13__4B(SOR__3__1y), ._12__4A(SOR__6__2y), ._11__4Y(SOR__11__4y));  // open: _7__GND, _14__Vcc, _10__3B, _9__3A, _8__3Y

  assign S3 = S;
endmodule
