// Logisim project assignment2_fixed.circ as structural Verilog: 29 circuits, main circuit FPA
// 10t16
module _10to16bit (
  input  [9:0] _10_bit_input,
  input  [4:0] exponent_input,
  output [15:0] _16_bit_output
);

  wire zero_checker_1_isone;

  zero_checker zero_checker_1 (.exponent(exponent_input), .isOne(zero_checker_1_isone));
  not not_1 (_16_bit_output[14], zero_checker_1_isone);

  assign {_16_bit_output[15], _16_bit_output[13:0]} = {1'b0, _10_bit_input, 4'b0000};
endmodule

// IPC
module Input_Processor (
  input  [15:0] A,
  output [15:0] _16_bit_significand,
  output [4:0] _5_bit_exponent,
  output Sign_Bit
);

  _10to16bit _10_to_16 (._10_bit_input(A[9:0]), .exponent_input(A[14:10]), ._16_bit_output(_16_bit_significand));

  assign _5_bit_exponent = A[14:10];
  assign Sign_Bit = A[15];
endmodule

// EDF
module Exponent_Differentiator (
  input  [4:0] Ea,
  input  [4:0] Eb,
  input  Sa,
  input  Sb,
  output Ea_Eb,
  output Ea_Eb_2,
  output [4:0] Ea_nEb,
  output [4:0] Larger_Exponent,
  output Largers_Sign,
  output Smallers_Sign
);

  wire subtractor_1_bout;
  wire [4:0] multiplexer_1_out;
  wire [5:5] subtractor_1_out;

  Comparator #(.width(5), .mode("unsigned")) comparator_1 (.a(Ea), .b(Eb), .gt(Ea_Eb), .eq(Ea_Eb_2));  // open: lt
  Multiplexer #(.width(5)) multiplexer_1 (.in0(Ea), .in1(Eb), .out(multiplexer_1_out), .sel(Ea_Eb), .en(1'b1));
  Multiplexer #(.width(5)) multiplexer_2 (.in0(Eb), .in1(Ea), .out(Larger_Exponent), .sel(Ea_Eb), .en(1'b1));
  Multiplexer multiplexer_3 (.in0(Sb), .in1(Sa), .out(Largers_Sign), .sel(Ea_Eb), .en(1'b1));
  Multiplexer multiplexer_4 (.in0(Sa), .in1(Sb), .out(Smallers_Sign), .sel(Ea_Eb), .en(1'b1));
  Subtractor #(.width(6)) subtractor_1 (
    .a({1'b0, Larger_Exponent}), .b({1'b0, multiplexer_1_out}), .out({subtractor_1_out[5], Ea_nEb}),
    .bout(subtractor_1_bout));  // open: bin
  // also tied to GND on the sheet: subtractor_1_bout
endmodule

// 1r
module _1_bit_right_shifter (
  input  [15:0] in_1,
  input  in_2,
  output [15:0] out_3
);

  Multiplexer #(.width(16)) multiplexer_1 (.in0(in_1), .in1({1'b0, in_1[15:1]}), .out(out_3), .sel(in_2), .en(1'b1));
endmodule

// 2r
module _2_bit_right_shifter (
  input  [15:0] in_1,
  input  in_2,
  output [15:0] out_3
);

  Multiplexer #(.width(16)) multiplexer_1 (.in0(in_1), .in1({2'b00, in_1[15:2]}), .out(out_3), .sel(in_2), .en(1'b1));
endmodule

// 4r
module _4_bit_right_shifter (
  input  [15:0] in_1,
  input  in_2,
  output [15:0] out_3
);

  Multiplexer #(.width(16)) multiplexer_1 (.in0(in_1), .in1({4'b0000, in_1[15:4]}), .out(out_3), .sel(in_2), .en(1'b1));
endmodule

// 8r
module _8_bit_right_shifter (
  input  [15:0] in_1,
  input  in_2,
  output [15:0] out_3
);

  Multiplexer #(.width(16)) multiplexer_1 (
    .in0(in_1), .in1({{8{1'b0}}, in_1[15:8]}), .out(out_3), .sel(in_2), .en(1'b1));
endmodule

// 16r
module _16_bit_right_shifter (
  input  [15:0] in_1,
  input  in_2,
  output [15:0] out_3
);

  Multiplexer #(.width(16)) multiplexer_1 (
    .in0(in_1), .in1({{15{1'b0}}, in_1[15]}), .out(out_3), .sel(in_2), .en(1'b1));
endmodule

// ARS
module arbitrary_rightshifter (
  input  [15:0] \input ,
  input  [4:0] Shift_Amount,
  output [15:0] Output
);

  wire [15:0] n1_bit_right_shifter_1_out_3, n2_bit_right_shifter_1_out_3, n4_bit_right_shifter_1_out_3,
       n8_bit_right_shifter_1_out_3;

  _1_bit_right_shifter u_1_bit_right_shifter_1 (
    .in_1(\input ), .in_2(Shift_Amount[0]), .out_3(n1_bit_right_shifter_1_out_3));
  _2_bit_right_shifter u_2_bit_right_shifter_1 (
    .in_1(n1_bit_right_shifter_1_out_3), .in_2(Shift_Amount[1]), .out_3(n2_bit_right_shifter_1_out_3));
  _4_bit_right_shifter u_4_bit_right_shifter_1 (
    .in_1(n2_bit_right_shifter_1_out_3), .in_2(Shift_Amount[2]), .out_3(n4_bit_right_shifter_1_out_3));
  _8_bit_right_shifter u_8_bit_right_shifter_1 (
    .in_1(n4_bit_right_shifter_1_out_3), .in_2(Shift_Amount[3]), .out_3(n8_bit_right_shifter_1_out_3));
  _16_bit_right_shifter u_16_bit_right_shifter_1 (
    .in_1(n8_bit_right_shifter_1_out_3), .in_2(Shift_Amount[4]), .out_3(Output));
endmodule

// RS
module Right_Shifter (
  input  [15:0] significand,
  input  [4:0] Exponent_Difference,
  output [15:0] \output ,
  output Sticky_Bit
);

  wire [31:0] shifter_1_out;

  Shifter_part #(.width(32), .shift("lr")) shifter_1 (
    .in({significand, {16{1'b0}}}), .\dist (Exponent_Difference), .out(shifter_1_out));
  arbitrary_rightshifter arbitrary_rightshifter_1 (
    .\input (significand), .Shift_Amount(Exponent_Difference), .Output(\output ));
  Comparator #(.width(16)) comparator_1 (.a(shifter_1_out[15:0]), .b({16{1'b0}}), .gt(Sticky_Bit));  // open: eq, lt
endmodule

// Iph
module Input (
  input  [15:0] A,
  input  [15:0] B,
  output [15:0] Larger_Fraction,
  output Sticky_Bit,
  output [15:0] Shifted_Smaller_s_Fraction,
  output [4:0] Larger_Exponent,
  output Larger_Sign,
  output [4:0] Exponent_DIfference,
  output Smaller_Sign
);

  wire comparator_1_gt, comparator_2_eq, exponent_differentiator_1_ea_eb, exponent_differentiator_1_ea_eb_2,
       input_processor_1_sign_bit, input_processor_2_sign_bit;
  wire [4:0] input_processor_1__5_bit_exponent, input_processor_2__5_bit_exponent;
  wire [15:0] input_processor_1__16_bit_significand, input_processor_2__16_bit_significand,
       multiplexer_1_out, multiplexer_2_out, multiplexer_3_out, multiplexer_5_out, multiplexer_6_out;

  Input_Processor input_processor_1 (
    .A(A), .Sign_Bit(input_processor_1_sign_bit),
    ._16_bit_significand(input_processor_1__16_bit_significand),
    ._5_bit_exponent(input_processor_1__5_bit_exponent));
  Input_Processor input_processor_2 (
    .A(B), .Sign_Bit(input_processor_2_sign_bit),
    ._16_bit_significand(input_processor_2__16_bit_significand),
    ._5_bit_exponent(input_processor_2__5_bit_exponent));
  Exponent_Differentiator exponent_differentiator_1 (
    .Ea(input_processor_1__5_bit_exponent), .Eb(input_processor_2__5_bit_exponent),
    .Sa(input_processor_1_sign_bit), .Sb(input_processor_2_sign_bit),
    .Ea_Eb(exponent_differentiator_1_ea_eb), .Ea_Eb_2(exponent_differentiator_1_ea_eb_2),
    .Larger_Exponent(Larger_Exponent), .Ea_nEb(Exponent_DIfference));  // open: Largers_Sign, Smallers_Sign
  Comparator #(.width(16), .mode("unsigned")) comparator_1 (
    .a(input_processor_1__16_bit_significand), .b(input_processor_2__16_bit_significand), .gt(comparator_1_gt));  // open: eq, lt
  Multiplexer #(.width(16), .enable("false")) multiplexer_1 (
    .in0(input_processor_2__16_bit_significand), .in1(input_processor_1__16_bit_significand),
    .out(multiplexer_1_out), .sel(exponent_differentiator_1_ea_eb));
  Multiplexer #(.width(16), .enable("false")) multiplexer_2 (
    .in0(input_processor_1__16_bit_significand), .in1(input_processor_2__16_bit_significand),
    .out(multiplexer_2_out), .sel(exponent_differentiator_1_ea_eb));
  Multiplexer #(.width(16), .enable("false")) multiplexer_3 (
    .in0(input_processor_2__16_bit_significand), .in1(input_processor_1__16_bit_significand),
    .out(multiplexer_3_out), .sel(comparator_1_gt));
  Multiplexer #(.width(16), .enable("false")) multiplexer_4 (
    .in0(multiplexer_1_out), .in1(multiplexer_3_out), .out(Larger_Fraction),
    .sel(exponent_differentiator_1_ea_eb_2));
  Multiplexer #(.width(16), .enable("false")) multiplexer_5 (
    .in0(input_processor_1__16_bit_significand), .in1(input_processor_2__16_bit_significand),
    .out(multiplexer_5_out), .sel(comparator_1_gt));
  Comparator #(.width(16), .mode("unsigned")) comparator_2 (
    .a(Larger_Fraction), .b(input_processor_1__16_bit_significand), .eq(comparator_2_eq));  // open: gt, lt
  Multiplexer #(.width(16), .enable("false")) multiplexer_6 (
    .in0(multiplexer_2_out), .in1(multiplexer_5_out), .out(multiplexer_6_out),
    .sel(exponent_differentiator_1_ea_eb_2));
  Right_Shifter right_shifter_1 (
    .significand(multiplexer_6_out), .Exponent_Difference(Exponent_DIfference),
    .\output (Shifted_Smaller_s_Fraction), .Sticky_Bit(Sticky_Bit));
  Multiplexer #(.enable("false")) multiplexer_7 (
    .in0(input_processor_2_sign_bit), .in1(input_processor_1_sign_bit), .out(Larger_Sign),
    .sel(comparator_2_eq));
  Multiplexer #(.enable("false")) multiplexer_8 (
    .in0(input_processor_1_sign_bit), .in1(input_processor_2_sign_bit), .out(Smaller_Sign),
    .sel(comparator_2_eq));
endmodule

// 1l
module _1_bit_left_shifter (
  input  [15:0] F,
  input  S,
  output [15:0] out_3
);

  Multiplexer #(.width(16)) multiplexer_1 (.in0(F), .in1({F[14:0], 1'b0}), .out(out_3), .sel(S), .en(1'b1));
endmodule

// 2l
module _2_bit_left_shifter (
  input  [15:0] F,
  input  S,
  output [15:0] out_3
);

  Multiplexer #(.width(16)) multiplexer_1 (.in0(F), .in1({F[13:0], 2'b00}), .out(out_3), .sel(S), .en(1'b1));
endmodule

// 4l
module _4_bit_left_shifter (
  input  [15:0] F,
  input  S,
  output [15:0] out_3
);

  Multiplexer #(.width(16)) multiplexer_1 (.in0(F), .in1({F[11:0], 4'b0000}), .out(out_3), .sel(S), .en(1'b1));
endmodule

// 8l
module _8_bit_left_shifter (
  input  [15:0] F,
  input  S,
  output [15:0] out_3
);

  Multiplexer #(.width(16)) multiplexer_1 (.in0(F), .in1({F[6:0], {9{1'b0}}}), .out(out_3), .sel(S), .en(1'b1));
endmodule

// 16l
module _16_bit_left_shifter (
  input  [15:0] F,
  input  S,
  output [15:0] out_3
);

  Multiplexer #(.width(16)) multiplexer_1 (.in0(F), .in1({F[0], {15{1'b0}}}), .out(out_3), .sel(S), .en(1'b1));
endmodule

module arbitrary_leftshifter (
  input  [15:0] Input,
  input  [4:0] Shift_Amount,
  output [15:0] Output
);

  wire [15:0] n1_bit_left_shifter_1_out_3, n2_bit_left_shifter_1_out_3, n4_bit_left_shifter_1_out_3,
       n8_bit_left_shifter_1_out_3;

  _1_bit_left_shifter u_1_bit_left_shifter_1 (.F(Input), .S(Shift_Amount[0]), .out_3(n1_bit_left_shifter_1_out_3));
  _2_bit_left_shifter u_2_bit_left_shifter_1 (
    .F(n1_bit_left_shifter_1_out_3), .S(Shift_Amount[1]), .out_3(n2_bit_left_shifter_1_out_3));
  _4_bit_left_shifter u_4_bit_left_shifter_1 (
    .F(n2_bit_left_shifter_1_out_3), .S(Shift_Amount[2]), .out_3(n4_bit_left_shifter_1_out_3));
  _8_bit_left_shifter u_8_bit_left_shifter_1 (
    .F(n4_bit_left_shifter_1_out_3), .S(Shift_Amount[3]), .out_3(n8_bit_left_shifter_1_out_3));
  _16_bit_left_shifter u_16_bit_left_shifter_1 (.F(n8_bit_left_shifter_1_out_3), .S(Shift_Amount[4]), .out_3(Output));
endmodule

module subtractor (
  input  [4:0] Ea,
  input  [9:0] Fa,
  input  [9:0] Fb,
  input  [4:0] Eb,
  output [4:0] Raw_Exp_Difference,
  output [9:0] Smaller,
  output [9:0] Greater
);

  wire comparator_1_gt;
  wire [4:0] multiplexer_1_out, multiplexer_2_out;

  Comparator #(.width(5)) comparator_1 (.a(Ea), .b(Eb), .gt(comparator_1_gt));  // open: eq, lt
  Multiplexer #(.width(5)) multiplexer_1 (
    .in0(Ea), .in1(Eb), .out(multiplexer_1_out), .sel(comparator_1_gt), .en(1'b1));
  Multiplexer #(.width(5)) multiplexer_2 (
    .in0(Eb), .in1(Ea), .out(multiplexer_2_out), .sel(comparator_1_gt), .en(1'b1));
  Subtractor #(.width(5)) subtractor_1 (
    .a(multiplexer_2_out), .b(multiplexer_1_out), .out(Raw_Exp_Difference));  // open: bin, bout
  Multiplexer #(.width(10)) multiplexer_3 (.in0(Fa), .in1(Fb), .out(Smaller), .sel(comparator_1_gt), .en(1'b1));
  Multiplexer #(.width(10)) multiplexer_4 (.in0(Fb), .in1(Fa), .out(Greater), .sel(comparator_1_gt), .en(1'b1));
endmodule

// NRM
module Normalizer (
  input  [15:0] significand_input,
  input  [4:0] exponent_input,
  output [4:0] normalized_Exponent,
  output [15:0] normalized_Significand,
  output underflow,
  output overflow
);

  wire A_S_overflow, A_S_underflow, and_1_out, priority_encoder_1_en_out, xor_1_out, zero_checker_1_isone;
  wire [3:0] multiplexer_1_out, priority_encoder_1_out, subtractor_1_out;
  wire [4:0] A_S_output_exponent, multiplexer_2_out;
  wire [15:0] arbitrary_leftshifter_1_output, multiplexer_4_out, n1_bit_right_shifter_1_out_3, Shifter_output;

  xor xor_1 (xor_1_out, significand_input[15], 1'b1);
  and and_1 (and_1_out, xor_1_out, priority_encoder_1_en_out);
  Priority_Encoder #(.select(4)) priority_encoder_1 (
    .in0(significand_input[0]), .in1(significand_input[1]), .in2(significand_input[2]),
    .in3(significand_input[3]), .in4(significand_input[4]), .in5(significand_input[5]),
    .in6(significand_input[6]), .in7(significand_input[7]), .in8(significand_input[8]),
    .in9(significand_input[9]), .in10(significand_input[10]), .in11(significand_input[11]),
    .in12(significand_input[12]), .in13(significand_input[13]), .in14(significand_input[14]), .in15(1'b0),
    .out(priority_encoder_1_out), .en_out(priority_encoder_1_en_out), .en_in(1'b1));  // open: gs
  arbitrary_leftshifter arbitrary_leftshifter_1 (
    .Input(significand_input), .Shift_Amount(exponent_input), .Output(arbitrary_leftshifter_1_output));
  Multiplexer #(.width(4), .disabled(0), .enable("false")) multiplexer_1 (
    .in0(priority_encoder_1_out), .in1(4'b1110), .out(multiplexer_1_out), .sel(priority_encoder_1_en_out));
  Shifter Shifter (
    .\input (significand_input), .shiftAmmount(multiplexer_2_out), .left_right(significand_input[15]),
    .\output (Shifter_output));
  _1_bit_right_shifter u_1_bit_right_shifter_1 (
    .in_1(arbitrary_leftshifter_1_output), .in_2(1'b1), .out_3(n1_bit_right_shifter_1_out_3));
  Subtractor #(.width(4)) subtractor_1 (.a(4'b1110), .b(multiplexer_1_out), .out(subtractor_1_out));  // open: bin, bout
  Multiplexer #(.width(5), .disabled(0), .enable("false")) multiplexer_2 (
    .in0({1'b0, subtractor_1_out}), .in1(5'b00001), .out(multiplexer_2_out), .sel(significand_input[15]));
  Multiplexer #(.width(5), .disabled(0), .enable("false")) multiplexer_3 (
    .in0(A_S_output_exponent), .in1({5{1'b0}}), .out(normalized_Exponent), .sel(and_1_out));
  Multiplexer #(.width(16), .disabled(0), .enable("false")) multiplexer_4 (
    .in0(Shifter_output), .in1({16{1'b0}}), .out(multiplexer_4_out), .sel(and_1_out));
  adder_sub_lib A_S (
    .input_exponent(exponent_input), .add_sub_amount(multiplexer_2_out), .underflow(A_S_underflow),
    .add_sub(significand_input[15]), .overflow(A_S_overflow), .output_exponent(A_S_output_exponent));
  zero_checker zero_checker_1 (.exponent(A_S_output_exponent), .isOne(zero_checker_1_isone));
  Multiplexer #(.disabled(0), .enable("false")) multiplexer_5 (
    .in0(A_S_underflow), .in1(1'b0), .out(underflow), .sel(and_1_out));
  Multiplexer #(.disabled(0), .enable("false")) multiplexer_6 (
    .in0(A_S_overflow), .in1(1'b0), .out(overflow), .sel(and_1_out));
  Multiplexer #(.width(16), .disabled(0), .enable("false")) multiplexer_7 (
    .in0(multiplexer_4_out), .in1(n1_bit_right_shifter_1_out_3), .out(normalized_Significand),
    .sel(zero_checker_1_isone));

  // Notes on the sheet:
  //   highest encoded value
  //   substractor
  //   right shift ammount
endmodule

// SHFT
module Shifter (
  input  [15:0] \input ,
  input  [4:0] shiftAmmount,
  input  left_right,
  output [15:0] \output 
);

  wire [15:0] arbitrary_leftshifter_1_output, arbitrary_rightshifter_1_output;

  arbitrary_leftshifter arbitrary_leftshifter_1 (
    .Input(\input ), .Shift_Amount(shiftAmmount), .Output(arbitrary_leftshifter_1_output));
  arbitrary_rightshifter arbitrary_rightshifter_1 (
    .\input (\input ), .Shift_Amount(shiftAmmount), .Output(arbitrary_rightshifter_1_output));
  Multiplexer #(.width(16), .disabled(0), .enable("false")) multiplexer_1 (
    .in0(arbitrary_leftshifter_1_output), .in1(arbitrary_rightshifter_1_output), .out(\output ),
    .sel(left_right));
endmodule

// A/S
module adder_sub_lib (
  input  [4:0] input_exponent,
  input  [4:0] add_sub_amount,
  input  add_sub,
  output underflow,
  output [4:0] output_exponent,
  output overflow
);

  wire adder_1_cout, not_1_out, one_checker_1_isone, or_1_out, or_2_out, subtractor_1_bout,
       zero_checker_1_isone;
  wire [4:0] adder_1_out, multiplexer_1_out, multiplexer_2_out, subtractor_1_out;

  Subtractor #(.width(5)) subtractor_1 (
    .a(input_exponent), .b(add_sub_amount), .out(subtractor_1_out), .bin(1'b0), .bout(subtractor_1_bout));
  Adder #(.width(5)) adder_1 (
    .a(input_exponent), .b(add_sub_amount), .out(adder_1_out), .cin(1'b0), .cout(adder_1_cout));
  or or_1 (or_1_out, adder_1_cout, one_checker_1_isone);
  zero_checker zero_checker_1 (.exponent(output_exponent), .isOne(zero_checker_1_isone));
  Multiplexer #(.width(5), .disabled(0), .enable("false")) multiplexer_1 (
    .in0(subtractor_1_out), .in1({5{1'b0}}), .out(multiplexer_1_out), .sel(subtractor_1_bout));
  Multiplexer #(.width(5), .disabled(0), .enable("false")) multiplexer_2 (
    .in0(adder_1_out), .in1({5{1'b1}}), .out(multiplexer_2_out), .sel(adder_1_cout));
  one_checker one_checker_1 (.exponent(output_exponent), .isOne(one_checker_1_isone));
  or or_2 (or_2_out, subtractor_1_bout, zero_checker_1_isone);
  not not_1 (not_1_out, add_sub);
  and and_1 (underflow, not_1_out, or_2_out);
  and and_2 (overflow, add_sub, or_1_out);
  Multiplexer #(.width(5), .disabled(0), .enable("false")) multiplexer_3 (
    .in0(multiplexer_1_out), .in1(multiplexer_2_out), .out(output_exponent), .sel(add_sub));
endmodule

// ZCK
module zero_checker (
  input  [4:0] exponent,
  output isOne
);

  nor nor_1 (isOne, exponent[0], exponent[1], exponent[2], exponent[3], exponent[4]);
endmodule

// OCK
module one_checker (
  input  [4:0] exponent,
  output isOne
);

  and and_1 (isOne, exponent[0], exponent[1], exponent[2], exponent[3], exponent[4]);
endmodule

// RN
module rounded_normalizer (
  input  [4:0] exponent_input,
  input  [15:0] significand_input,
  output overflow,
  output [4:0] normalized_Exponent,
  output [15:0] normalized_Significand
);

  wire adder_1_cout, one_checker_1_isone, one_checker_2_isone;
  wire [15:0] multiplexer_1_out, n1_bit_right_shifter_1_out_3;

  Adder #(.width(5)) adder_1 (
    .a(exponent_input), .b({5{1'b0}}), .out(normalized_Exponent), .cin(significand_input[15]),
    .cout(adder_1_cout));
  _1_bit_right_shifter u_1_bit_right_shifter_1 (
    .in_1(significand_input), .in_2(1'b1), .out_3(n1_bit_right_shifter_1_out_3));
  Multiplexer #(.width(16), .disabled(0), .enable("false")) multiplexer_1 (
    .in0(significand_input), .in1(n1_bit_right_shifter_1_out_3), .out(multiplexer_1_out),
    .sel(significand_input[15]));
  one_checker one_checker_1 (.exponent(normalized_Exponent), .isOne(one_checker_1_isone));
  one_checker one_checker_2 (.exponent(normalized_Exponent), .isOne(one_checker_2_isone));
  or or_1 (overflow, one_checker_1_isone, adder_1_cout);
  Multiplexer #(.width(16), .disabled(0), .enable("false")) multiplexer_2 (
    .in0(multiplexer_1_out), .in1({16{1'b0}}), .out(normalized_Significand), .sel(one_checker_2_isone));
endmodule

// Rndr
module rounder (
  input  Sticky_Bit,
  input  [15:0] significand,
  output [15:0] rounded_significand
);

  wire and_1_out, or_1_out, or_2_out;
  wire [10:0] multiplexer_1_out;

  or or_1 (or_1_out, significand[0], Sticky_Bit, significand[1]);
  or or_2 (or_2_out, or_1_out, significand[2], significand[4]);
  and and_1 (and_1_out, significand[3], or_2_out);
  Multiplexer #(.width(11)) multiplexer_1 (
    .in0({11{1'b0}}), .in1(11'h1), .out(multiplexer_1_out), .sel(and_1_out), .en(1'b1));
  Adder #(.width(11)) adder_1 (
    .a(significand[14:4]), .b(multiplexer_1_out), .out(rounded_significand[14:4]),
    .cout(rounded_significand[15]));  // open: cin

  assign rounded_significand[3:0] = 4'b0000;
endmodule

// Add
module adder16bit (
  input  sign_A,
  input  [15:0] A,
  input  [15:0] B,
  input  sign_B,
  output Carry_Out,
  output [15:0] adder_result,
  output Output_Sign
);

  wire comparator_1_eq, comparator_1_lt, multiplexer_3_out, multiplexer_4_out, xor_1_out, xor_2_out;
  wire [15:0] adder_1_out, multiplexer_1_out, negator_1_out, subtractor_1_out;

  xor xor_1 (xor_1_out, sign_A, sign_B);
  Adder #(.width(16)) adder_1 (.a(A), .b(B), .out(adder_1_out), .cin(1'b0), .cout(Carry_Out));
  Subtractor #(.width(16)) subtractor_1 (.a(A), .b(B), .out(subtractor_1_out));  // open: bin, bout
  Comparator #(.width(16)) comparator_1 (.a(A), .b(B), .eq(comparator_1_eq), .lt(comparator_1_lt));  // open: gt
  Negator #(.width(16)) negator_1 (.in(subtractor_1_out), .out(negator_1_out));
  Multiplexer #(.width(16), .disabled(0), .enable("false")) multiplexer_1 (
    .in0(subtractor_1_out), .in1(negator_1_out), .out(multiplexer_1_out), .sel(comparator_1_lt));
  Multiplexer #(.width(16), .disabled(0), .enable("false")) multiplexer_2 (
    .in0(adder_1_out), .in1(multiplexer_1_out), .out(adder_result), .sel(xor_1_out));
  Multiplexer #(.disabled(0), .enable("false")) multiplexer_3 (
    .in0(sign_A), .in1(sign_B), .out(multiplexer_3_out), .sel(comparator_1_lt));
  Multiplexer #(.disabled(0), .enable("false")) multiplexer_4 (
    .in0(multiplexer_3_out), .in1(1'b0), .out(multiplexer_4_out), .sel(comparator_1_eq));
  xor xor_2 (xor_2_out, xor_1_out, sign_B);
  Multiplexer #(.disabled(0), .enable("false")) multiplexer_5 (
    .in0(xor_2_out), .in1(multiplexer_4_out), .out(Output_Sign), .sel(xor_1_out));
endmodule

// OPH
module output_handler (
  input  [9:0] Significand,
  input  [4:0] exponent,
  input  S,
  output [15:0] Output
);


  assign Output = {S, exponent, Significand};
endmodule

module FPA (
  input  [15:0] A,
  input  [15:0] B,
  output [15:0] Output,
  output Overflow,
  output Underflow
);

  wire input_1_larger_sign, input_1_smaller_sign, input_1_sticky_bit, normalizer_1_overflow,
       rounded_normalizer_1_overflow;
  wire [4:0] input_1_larger_exponent, normalizer_1_normalized_exponent;
  wire [15:0] adder16bit_1_adder_result, input_1_larger_fraction, input_1_shifted_smaller_s_fraction,
       normalizer_1_normalized_significand, rounded_normalizer_1_normalized_significand,
       rounder_1_rounded_significand;

  Input input_1 (
    .A(A), .B(B), .Larger_Sign(input_1_larger_sign), .Sticky_Bit(input_1_sticky_bit),
    .Larger_Exponent(input_1_larger_exponent), .Larger_Fraction(input_1_larger_fraction),
    .Shifted_Smaller_s_Fraction(input_1_shifted_smaller_s_fraction), .Smaller_Sign(input_1_smaller_sign));  // open: Exponent_DIfference
  adder16bit adder16bit_1 (
    .sign_A(input_1_larger_sign), .A(input_1_larger_fraction), .B(input_1_shifted_smaller_s_fraction),
    .sign_B(input_1_smaller_sign), .adder_result(adder16bit_1_adder_result), .Output_Sign(Output[15]));  // open: Carry_Out
  Normalizer normalizer_1 (
    .significand_input(adder16bit_1_adder_result), .exponent_input(input_1_larger_exponent),
    .underflow(Underflow), .overflow(normalizer_1_overflow),
    .normalized_Exponent(normalizer_1_normalized_exponent),
    .normalized_Significand(normalizer_1_normalized_significand));
  rounder rounder_1 (
    .significand(normalizer_1_normalized_significand), .Sticky_Bit(input_1_sticky_bit),
    .rounded_significand(rounder_1_rounded_significand));
  rounded_normalizer rounded_normalizer_1 (
    .exponent_input(normalizer_1_normalized_exponent), .significand_input(rounder_1_rounded_significand),
    .overflow(rounded_normalizer_1_overflow), .normalized_Exponent(Output[14:10]),
    .normalized_Significand({rounded_normalizer_1_normalized_significand[15:14], Output[9:0], rounded_normalizer_1_normalized_significand[3:0]}));
  or or_1 (Overflow, normalizer_1_overflow, rounded_normalizer_1_overflow);
endmodule

module hjb (
  input  [15:0] in_1,
  input  [15:0] in_2,
  input  [15:0] in_3,
  input  in_4,
  input  [15:0] in_5,
  input  [15:0] in_6,
  input  in_7,
  output out_8,
  output [15:0] out_9,
  output [15:0] out_10,
  output out_11
);

  rounded_normalizer rounded_normalizer_1 (
    .significand_input(in_1), .overflow(out_8));  // open: exponent_input, normalized_Exponent, normalized_Significand
  rounder rounder_1 (.significand(in_2), .rounded_significand(out_9));  // open: Sticky_Bit
  Normalizer normalizer_1 (.significand_input(in_3));  // open: exponent_input, underflow, overflow, normalized_Exponent, normalized_Significand
  adder16bit adder16bit_1 (
    .sign_A(in_4), .A(in_5), .B(in_6), .sign_B(in_7), .adder_result(out_10), .Output_Sign(out_11));  // open: Carry_Out
endmodule
