// Logisim project ALU_works.circ as structural Verilog: 1 circuit, main circuit ALU
module ALU (
  input  [3:0] A,
  input  [3:0] B,
  input  [2:0] ALU_control,
  output [3:0] ALU_result,
  output Zero_flag
);

  wire or_2_out;
  wire [3:0] adder_1_out, and_1_out, multiplexer_2_out, multiplexer_3_out, nor_1_out, or_1_out,
       shifter_1_out, shifter_2_out, subtractor_1_out;

  Adder #(.width(4)) adder_1 (.a(A), .b(B), .out(adder_1_out));  // open: cin, cout
  Subtractor #(.width(4)) subtractor_1 (.a(A), .b(B), .out(subtractor_1_out));  // open: bin, bout
  assign and_1_out = A & B;  // AND_Gate and_1, 4 bits wide
  assign or_1_out = A | B;  // OR_Gate or_1, 4 bits wide
  assign nor_1_out = ~(A | B);  // NOR_Gate nor_1, 4 bits wide
  Multiplexer #(.select(3), .width(4)) multiplexer_1 (
    .in0(adder_1_out), .in1(subtractor_1_out), .in2(and_1_out), .in3(or_1_out), .in4(nor_1_out),
    .in5(multiplexer_2_out), .in6(multiplexer_3_out), .out(ALU_result), .sel(ALU_control));  // open: in7
  or or_2 (or_2_out, B[2], B[3]);
  Shifter #(.width(4)) shifter_1 (.in(A), .\dist (B[1:0]), .out(shifter_1_out));
  Shifter #(.shift("lr"), .width(4)) shifter_2 (.in(A), .\dist (B[1:0]), .out(shifter_2_out));
  nor nor_2 (Zero_flag, ALU_result[0], ALU_result[1], ALU_result[2], ALU_result[3]);
  Multiplexer #(.width(4)) multiplexer_2 (.in0(shifter_1_out), .in1(4'b0000), .out(multiplexer_2_out), .sel(or_2_out));
  Multiplexer #(.width(4)) multiplexer_3 (.in0(shifter_2_out), .in1(4'b0000), .out(multiplexer_3_out), .sel(or_2_out));
endmodule
