// Logisim project Control_works.circ as structural Verilog: 1 circuit, main circuit Control_Unit
module Control_Unit (
  input  [3:0] OpCode,
  output RegDst,
  output ALUSrc,
  output MemToReg,
  output RegWrite,
  output MemRead,
  output MemWrite,
  output Branch,
  output BranchNot,
  output Jump,
  output [2:0] ALUOp,
  output IsShift,
  output IsSubi
);

  ROM #(.addrWidth(4), .dataWidth(14)) rom_1 (
    .addr(OpCode),
    .data({IsSubi, IsShift, ALUOp, Jump, BranchNot, Branch, MemWrite, MemRead, RegWrite, MemToReg, ALUSrc, RegDst}));

  // Notes on the sheet:
  //   contents of rom_1 (hex, n*v repeats v):
  //   1a08 9 209 809 280 1e 409 22 100 a 1c08 220a 240 40a 60a 609
endmodule
