// Logisim project Final_design.circ as structural Verilog: 1 circuit, main circuit Full_circuit
module Full_circuit (
  output [3:0] out_1
);

  wire alu_1_zero_flag, clock_1_out, comparator_1_eq, demultiplexer_1_out0, demultiplexer_1_out1,
       instrcution_fetch_1_alusrc, instrcution_fetch_1_isshift, instrcution_fetch_1_memread,
       instrcution_fetch_1_memtoreg, instrcution_fetch_1_memwrite, instrcution_fetch_1_regdst,
       instrcution_fetch_1_regwrite, or_1_out;
  wire [2:0] instrcution_fetch_1_aluop;
  wire [3:0] alu_1_alu_result, instrcution_fetch_1_dstsrc, instrcution_fetch_1_immval,
       instrcution_fetch_1_r1_src, instrcution_fetch_1_r2_src, multiplexer_1_out, multiplexer_2_out,
       multiplexer_3_out, multiplexer_4_out, multiplexer_5_out, ram_2_dout, register_file_1_r1_data,
       register_file_1_r2_data;

  Instrcution_fetch instrcution_fetch_1 (
    .Zero_flag_in(alu_1_zero_flag), .in_2(1'b1), .clk(clock_1_out), .ImmVal(instrcution_fetch_1_immval),
    .DstSrc(instrcution_fetch_1_dstsrc), .R1_src(instrcution_fetch_1_r1_src),
    .RegDst(instrcution_fetch_1_regdst), .R2_src(instrcution_fetch_1_r2_src),
    .ALUsrc(instrcution_fetch_1_alusrc), .MemToReg(instrcution_fetch_1_memtoreg),
    .RegWrite(instrcution_fetch_1_regwrite), .MemRead(instrcution_fetch_1_memread),
    .MemWrite(instrcution_fetch_1_memwrite), .ALUOp(instrcution_fetch_1_aluop),
    .IsShift(instrcution_fetch_1_isshift));  // open: Branch, BranchNot, Jump, IsSubi
  Multiplexer #(.width(4)) multiplexer_1 (
    .in0(instrcution_fetch_1_r2_src), .in1(instrcution_fetch_1_dstsrc), .out(multiplexer_1_out),
    .sel(instrcution_fetch_1_regdst));
  Multiplexer #(.width(4)) multiplexer_2 (
    .in0(instrcution_fetch_1_r2_src), .in1(instrcution_fetch_1_dstsrc), .out(multiplexer_2_out),
    .sel(instrcution_fetch_1_isshift));
  Clock clock_1 (.out(clock_1_out));
  Comparator #(.width(4)) comparator_1 (
    .a(instrcution_fetch_1_r1_src), .b(4'b0110), .eq(comparator_1_eq));  // open: gt, lt
  Register_File register_file_1 (
    .W_data(multiplexer_4_out), .R1_address(instrcution_fetch_1_r1_src), .R2_address(multiplexer_2_out),
    .W_address(multiplexer_1_out), .RegWrite(instrcution_fetch_1_regwrite), .Clk(clock_1_out),
    .R1_data(register_file_1_r1_data), .R2_data(register_file_1_r2_data));
  Multiplexer #(.width(4)) multiplexer_3 (
    .in0(register_file_1_r2_data), .in1(instrcution_fetch_1_immval), .out(multiplexer_3_out), .sel(or_1_out));
  or or_1 (or_1_out, instrcution_fetch_1_alusrc, instrcution_fetch_1_isshift);
  Demultiplexer demultiplexer_1 (
    .out0(demultiplexer_1_out0), .out1(demultiplexer_1_out1), .in(instrcution_fetch_1_memwrite),
    .sel(comparator_1_eq));
  ALU alu_1 (
    .A(register_file_1_r1_data), .B(multiplexer_3_out), .ALU_control(instrcution_fetch_1_aluop),
    .ALU_result(alu_1_alu_result), .Zero_flag(alu_1_zero_flag));
  Multiplexer #(.width(4)) multiplexer_4 (
    .in0(alu_1_alu_result), .in1(multiplexer_5_out), .out(multiplexer_4_out),
    .sel(instrcution_fetch_1_memtoreg));
  RAM #(.addrWidth(4), .asyncread("true"), .dataWidth(4)) ram_1 (
    .addr(alu_1_alu_result), .we(demultiplexer_1_out0), .oe(instrcution_fetch_1_memread), .clk(clock_1_out),
    .din(register_file_1_r2_data), .dout(out_1));
  RAM #(.addrWidth(4), .asyncread("true"), .dataWidth(4)) ram_2 (
    .addr(alu_1_alu_result), .we(demultiplexer_1_out1), .oe(instrcution_fetch_1_memread), .clk(clock_1_out),
    .din(register_file_1_r2_data), .dout(ram_2_dout));
  Multiplexer #(.width(4)) multiplexer_5 (
    .in0(out_1), .in1(ram_2_dout), .out(multiplexer_5_out), .sel(comparator_1_eq));
endmodule
