// Logisim project Instruction.circ as structural Verilog: 1 circuit, main circuit Instrcution_fetch
module Instrcution_fetch (
  input  Zero_flag_in,
  input  in_2,
  input  clk,
  output [3:0] ImmVal,
  output [3:0] DstSrc,
  output [3:0] R1_src,
  output RegDst,
  output [3:0] R2_src,
  output ALUsrc,
  output MemToReg,
  output RegWrite,
  output MemRead,
  output MemWrite,
  output Branch,
  output BranchNot,
  output Jump,
  output [2:0] ALUOp,
  output IsShift,
  output IsSubi
);

  wire and_1_out, and_2_out, not_1_out, or_1_out;
  wire [3:0] rom_1_data;
  wire [7:0] adder_1_out, adder_2_out, bit_extender_1_out, multiplexer_1_out, multiplexer_2_out, register_1_q;

  Register register_1 (.D(multiplexer_2_out), .en(in_2), .clk(clk), .Q(register_1_q));  // open: clr
  ROM #(.dataWidth(16)) rom_1 (.addr(register_1_q), .data({rom_1_data, R1_src, R2_src, DstSrc}));
  Adder adder_1 (.a(register_1_q), .b(8'h1), .out(adder_1_out));  // open: cin, cout
  Multiplexer #(.width(8)) multiplexer_1 (
    .in0(adder_1_out), .in1(adder_2_out), .out(multiplexer_1_out), .sel(or_1_out));
  Multiplexer #(.width(8)) multiplexer_2 (
    .in0(multiplexer_1_out), .in1({R1_src, R2_src}), .out(multiplexer_2_out), .sel(Jump));
  not not_1 (not_1_out, Zero_flag_in);
  Control_Unit control_unit_1 (
    .OpCode(rom_1_data), .RegDst(RegDst), .ALUSrc(ALUsrc), .MemToReg(MemToReg), .RegWrite(RegWrite),
    .MemRead(MemRead), .MemWrite(MemWrite), .Branch(Branch), .BranchNot(BranchNot), .Jump(Jump),
    .ALUOp(ALUOp), .IsShift(IsShift), .IsSubi(IsSubi));
  and and_1 (and_1_out, Branch, Zero_flag_in);
  and and_2 (and_2_out, BranchNot, not_1_out);
  assign bit_extender_1_out = {{4{DstSrc[3]}}, DstSrc};  // Bit_Extender bit_extender_1
  or or_1 (or_1_out, and_1_out, and_2_out);
  Adder adder_2 (.a(bit_extender_1_out), .b(adder_1_out), .out(adder_2_out));  // open: cin, cout

  assign ImmVal = DstSrc;

  // Notes on the sheet:
  //   contents of rom_1 (hex, n*v repeats v):
  //   966f 9021 9033 1231 1134 1125 7323 222 c121 81f0 2415 b441 a441 5323 6241 f452 81d0 966f 7610 966f
  //   7620 e114 5610 9661 d330 5630 9661 3333 81f0 c131 8110
endmodule
