// Logisim project Register_Memory.circ as structural Verilog: 1 circuit, main circuit Register_File
module Register_File (
  input  [3:0] W_data,
  input  [3:0] R1_address,
  input  [3:0] R2_address,
  input  [3:0] W_address,
  input  RegWrite,
  input  Clk,
  output [3:0] R1_data,
  output [3:0] R2_data
);

  wire demultiplexer_1_out1, demultiplexer_1_out2, demultiplexer_1_out3, demultiplexer_1_out4,
       demultiplexer_1_out5, demultiplexer_1_out6;
  wire [3:0] sp_q, t0_q, t1_q, t2_q, t3_q, t4_q;

  Multiplexer #(.select(4), .width(4)) multiplexer_1 (
    .in0(4'b0000), .in1(t0_q), .in2(t1_q), .in3(t2_q), .in4(t3_q), .in5(t4_q), .in6(sp_q), .in7(4'b0000),
    .in8(4'b0000), .in9(4'b0000), .in10(4'b0000), .in11(4'b0000), .in12(4'b0000), .in13(4'b0000),
    .in14(4'b0000), .in15(4'b0000), .out(R1_data), .sel(R1_address));
  Multiplexer #(.select(4), .width(4)) multiplexer_2 (
    .in0(4'b0000), .in1(t0_q), .in2(t1_q), .in3(t2_q), .in4(t3_q), .in5(t4_q), .in6(sp_q), .in7(4'b0000),
    .in8(4'b0000), .in9(4'b0000), .in10(4'b0000), .in11(4'b0000), .in12(4'b0000), .in13(4'b0000),
    .in14(4'b0000), .in15(4'b0000), .out(R2_data), .sel(R2_address));
  Demultiplexer #(.select(4)) demultiplexer_1 (
    .out1(demultiplexer_1_out1), .out2(demultiplexer_1_out2), .out3(demultiplexer_1_out3),
    .out4(demultiplexer_1_out4), .out5(demultiplexer_1_out5), .out6(demultiplexer_1_out6), .in(RegWrite),
    .sel(W_address));  // open: out0, out7, out8, out9, out10, out11, out12, out13, out14, out15
  Register #(.width(4)) t0 (.D(W_data), .en(demultiplexer_1_out1), .clk(Clk), .Q(t0_q));  // open: clr
  Register #(.width(4)) t1 (.D(W_data), .en(demultiplexer_1_out2), .clk(Clk), .Q(t1_q));  // open: clr
  Register #(.width(4)) t2 (.D(W_data), .en(demultiplexer_1_out3), .clk(Clk), .Q(t2_q));  // open: clr
  Register #(.width(4)) t3 (.D(W_data), .en(demultiplexer_1_out4), .clk(Clk), .Q(t3_q));  // open: clr
  Register #(.width(4)) t4 (.D(W_data), .en(demultiplexer_1_out5), .clk(Clk), .Q(t4_q));  // open: clr
  Register #(.width(4)) sp (.D(W_data), .en(demultiplexer_1_out6), .clk(Clk), .Q(sp_q));  // open: clr
endmodule
